# Fritzing sketch wiring_diagram (saved by Fritzing 0.9.2b)

parts:
  Part1 = Pro Trinket 3.3V
  MIC1 = MAX4466 Electret Microphone Breakout Board
  U1 = LIPO-2000mAh [package=lipo-2000]
  S1 = Toggle Switch [package=THT]
  C1 = Electrolytic Capacitor [capacitance=1000μF package="1010 [SMD, electrolytic]"]
  NEOPIXEL1 = Neopixel Strip -- White (60/m)
  NEOPIXEL2 = Neopixel Strip -- White (60/m)
  J1 = Piezo Speaker

nets:
  N1: Part1.VBAT, S1.COM, C1.+, NEOPIXEL1.DI, NEOPIXEL2.DI
  GND: Part1.GND, MIC1.GND, U1.-, C1.-, NEOPIXEL1.GND, NEOPIXEL2.GND, J1.pin1
  +3V3: Part1.+3V3, MIC1.VCC
  N2: Part1.D6, NEOPIXEL2.+5V
  N3: Part1.D5, NEOPIXEL1.+5V
  N4: Part1.D4, J1.pin2
  N5: Part1.A7, MIC1.out
  N6: U1.+, S1.L1

custom parts:
  Pro Trinket 3.3V: The Pro Trinket 3.3V is like an Arduino Pro Mini with more pins and USB included. However, it uses 3V logic and 12MHz clock which means it's good when you want a lower-power and lower-voltage setup. Built with the common core Arduino chip, the ATmega328p, it has 18 GPIO, 2 extra analog inputs, 28K of flash, and 2K of RAM. It has onboard USB bootloading support with Optiboot support, so you can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
  MAX4466 Electret Microphone Breakout Board: MAX4466 Electrec Microphone Breakout Board
  Neopixel Strip -- White (60/m): Neopixel Strip, White, 60 pixels per meter.
